// Logisim project alu.circ as structural Verilog: 1 circuit, main circuit alu
module alu (
  input  [31:0] A,
  input  [31:0] B,
  input  [3:0] ALUSel,
  output [31:0] Result
);

  wire [4:0] bit_extender_1_out, bit_extender_2_out, bit_extender_3_out;
  wire [31:0] add0, and0, divu0, mul0, mulh0, mulhu0, or0, remu0, sll0, slt0, sra0, srl0, sub0, xor0;

  Bit_Extender #(.in_width(32), .out_width(5), .\type ("zero")) bit_extender_1 (.in(B), .out(bit_extender_1_out));
  Bit_Extender #(.in_width(32), .out_width(5), .\type ("zero")) bit_extender_2 (.in(B), .out(bit_extender_2_out));
  Bit_Extender #(.in_width(32), .out_width(5), .\type ("zero")) bit_extender_3 (.in(B), .out(bit_extender_3_out));
  Adder #(.width(32)) adder_1 (.a(A), .b(B), .out(add0));  // open: cin, cout
  assign and0 = A & B;  // AND_Gate and_1, 32 bits wide
  assign or0 = A | B;  // OR_Gate or_1, 32 bits wide
  assign xor0 = A ^ B;  // XOR_Gate xor_1, 32 bits wide
  Shifter #(.width(32), .shift("lr")) shifter_1 (.in(A), .\dist (bit_extender_1_out), .out(srl0));
  Shifter #(.width(32), .shift("ar")) shifter_2 (.in(A), .\dist (bit_extender_2_out), .out(sra0));
  Shifter #(.width(32)) shifter_3 (.in(A), .\dist (bit_extender_3_out), .out(sll0));
  Shifter #(.width(32), .shift("lr")) shifter_4 (.in(sub0), .\dist ({5{1'b1}}), .out(slt0));
  Subtractor #(.width(32)) subtractor_1 (.a(A), .b(B), .out(sub0));  // open: bin, bout
  Divider #(.width(32)) divider_1 (.a(A), .b(B), .out(divu0), .rem(remu0));  // open: upper
  Multiplexer #(.select(4), .width(32), .enable("false")) multiplexer_1 (
    .in0(add0), .in1(and0), .in2(or0), .in3(xor0), .in4(srl0), .in5(sra0), .in6(sll0), .in7(slt0),
    .in8(divu0), .in9(remu0), .in10(mul0), .in11(mulhu0), .in12(sub0), .in13(B), .in14(mulh0), .out(Result),
    .sel(ALUSel));  // open: in15

  // Notes on the sheet:
  //   INPUTS to your circuit
  //   DON'T CHANGE THE LOCATIONS OF THE INPUTS AND OUTPUTS!
  //   OUTPUT from your circuit
endmodule
