// Logisim project control_logic.circ as structural Verilog: 1 circuit, main circuit control_logic
module control_logic (
  input  [31:0] inst,
  input  BrEq,
  input  BrLt,
  output PCSel,
  output RegWEn,
  output [2:0] ImmSel,
  output BrUn,
  output ASel,
  output BSel,
  output [3:0] ALUSel,
  output MemRW,
  output [1:0] WBSel
);

  wire and_2_out, and_3_out;
  wire [1:0] multiplexer_3_out, multiplexer_4_out;
  wire [2:0] adder_1_out, adder_2_out, multiplexer_1_out, multiplexer_2_out;

  Adder #(.width(3)) adder_1 (.a(inst[6:4]), .b(3'b001), .out(adder_1_out));  // open: cin, cout
  Adder #(.width(3)) adder_2 (.a(inst[6:4]), .b(3'b111), .out(adder_2_out));  // open: cin, cout
  or or_1 (RegWEn, inst[2], inst[4], ~inst[5]);  // OR_Gate
  and and_1 (MemRW, ~inst[4], inst[5], ~inst[6]);  // AND_Gate
  and and_2 (and_2_out, ~inst[4], ~inst[5], ~inst[6]);  // AND_Gate
  and and_3 (and_3_out, inst[2], inst[5], inst[6]);
  Multiplexer #(.width(3), .enable("false")) multiplexer_1 (
    .in0(inst[6:4]), .in1(adder_1_out), .out(multiplexer_1_out), .sel(inst[2]));
  Multiplexer #(.width(3), .enable("false")) multiplexer_2 (
    .in0(inst[6:4]), .in1(adder_2_out), .out(multiplexer_2_out), .sel(inst[3]));
  Multiplexer #(.width(2), .enable("false")) multiplexer_3 (
    .in0(2'b00), .in1(2'b01), .out(multiplexer_3_out), .sel(and_2_out));
  Multiplexer #(.width(2), .enable("false")) multiplexer_4 (
    .in0(2'b00), .in1(2'b10), .out(multiplexer_4_out), .sel(and_3_out));
  // Probe on ImmSel
  Multiplexer #(.width(3), .enable("false")) multiplexer_5 (
    .in0(multiplexer_1_out), .in1(multiplexer_2_out), .out(ImmSel), .sel(inst[3]));
  // Probe on WBSel
  Multiplexer #(.width(2), .enable("false")) multiplexer_6 (
    .in0(multiplexer_3_out), .in1(multiplexer_4_out), .out(WBSel), .sel(and_3_out));

  assign ALUSel = 4'b0000;
  assign ASel = 1'b0;
  assign BSel = 1'b1;
  assign PCSel = 1'b0;

  // Other names for the same wires on the sheet: op[6:0] = inst[6:0]; rd[4:0] = inst[11:7]; func3[2:0] = inst[14:12];
  //   r1[4:0] = inst[19:15]; r2[4:0] = inst[24:20]; func7[6:0] = inst[31:25]

  // Notes on the sheet:
  //   B-Type and S-Type
  //   S-Type
  //   I-Type: load cmd
  //   jal and jalr cmd
  //   INPUTS to your circuit
  //   DON'T CHANGE THE LOCATIONS OF THE INPUTS AND OUTPUTS!
  //   OUTPUT from your circuit
endmodule
